// Logisim project decodeur_7_segments.circ as structural Verilog
module main (
  input  a,
  input  b,
  input  c,
  input  d,
  input  e,
  input  f,
  input  g
);

  wire p;

  _7_Segment_Display u_7_segment_display_1 (.g(g), .f(f), .a(a), .b(b), .e(e), .d(d), .c(c), .dp(p));

  // Notes on the sheet:
  //   pins d'entrée
  //   Tester les boutons de a à f en sélectionnant le mode interactif (petite main en haut à gauche)
  //   <= les tunnels sont des connections à distance =>
  //   les labels doivent être identiques pour être connectés
endmodule

module Decodeur_7_seg (
  input  e3,
  input  e2,
  input  e1,
  input  e0,
  output a,
  output b,
  output c,
  output d,
  output e,
  output f,
  output g
);

  wire and_1_out, and_2_out, and_3_out, and_4_out, and_5_out, and_6_out, and_7_out, and_8_out, and_9_out,
       and_10_out, and_11_out, and_12_out, and_13_out, and_14_out, and_15_out, and_16_out, and_17_out,
       and_18_out, and_19_out, and_20_out, and_21_out, and_22_out, and_23_out, and_24_out, and_25_out,
       and_26_out, and_27_out, and_28_out, and_29_out, and_30_out, and_31_out, and_32_out, and_33_out,
       and_34_out, and_35_out, not_1_out, not_2_out, not_3_out, not_4_out;

  not not_1 (not_1_out, e3);
  not not_2 (not_2_out, e2);
  not not_3 (not_3_out, e1);
  not not_4 (not_4_out, e0);
  and and_1 (and_1_out, not_2_out, not_4_out);
  and and_2 (and_2_out, not_1_out, e1);
  and and_3 (and_3_out, not_1_out, e2, e0);
  and and_4 (and_4_out, e2, e1);
  and and_5 (and_5_out, e3, not_2_out, not_3_out);
  and and_6 (and_6_out, e3, not_4_out);
  and and_7 (and_7_out, not_1_out, not_2_out);
  and and_8 (and_8_out, not_1_out, not_3_out, not_4_out);
  and and_9 (and_9_out, not_2_out, not_4_out);
  and and_10 (and_10_out, not_1_out, e1, e0);
  and and_11 (and_11_out, e3, not_3_out, e0);
  and and_12 (and_12_out, not_1_out, not_3_out);
  and and_13 (and_13_out, not_1_out, e0);
  and and_14 (and_14_out, not_3_out, e0);
  and and_15 (and_15_out, not_1_out, e2);
  and and_16 (and_16_out, e3, not_2_out);
  and and_17 (and_17_out, not_1_out, not_2_out, not_4_out);
  and and_18 (and_18_out, not_2_out, e1, e0);
  and and_19 (and_19_out, e2, not_3_out, e0);
  and and_20 (and_20_out, e2, e1, not_4_out);
  and and_21 (and_21_out, e3, not_3_out);
  and and_22 (and_22_out, not_2_out, not_4_out);
  and and_23 (and_23_out, e1, not_4_out);
  and and_24 (and_24_out, e3, e1);
  and and_25 (and_25_out, e3, e2);
  and and_26 (and_26_out, not_3_out, not_4_out);
  and and_27 (and_27_out, not_1_out, e2, not_3_out);
  and and_28 (and_28_out, e2, not_4_out);
  and and_29 (and_29_out, e3, not_2_out);
  and and_30 (and_30_out, e3, e1);
  and and_31 (and_31_out, not_2_out, e1);
  and and_32 (and_32_out, e1, not_4_out);
  and and_33 (and_33_out, not_1_out, e2, not_3_out);
  and and_34 (and_34_out, e3, not_2_out);
  and and_35 (and_35_out, e3, e0);
  or or_1 (a, and_1_out, and_2_out, and_3_out, and_4_out, and_5_out, and_6_out);
  or or_2 (b, and_7_out, and_8_out, and_9_out, and_10_out, and_11_out);
  or or_3 (c, and_12_out, and_13_out, and_14_out, and_15_out, and_16_out);
  or or_4 (d, and_17_out, and_18_out, and_19_out, and_20_out, and_21_out);
  or or_5 (e, and_22_out, and_23_out, and_24_out, and_25_out);
  or or_6 (f, and_26_out, and_27_out, and_28_out, and_29_out, and_30_out);
  or or_7 (g, and_31_out, and_32_out, and_33_out, and_34_out, and_35_out);
endmodule

module decodeur_et_afficheur (
);

  wire A, a_t, B, b_t, C, c_t, clock_1_out, D, d_t, E, e_t, F, f_t, G, g_t;
  wire [7:0] counter_1_q;

  Clock clock_1 (.out(clock_1_out));
  Counter counter_1 (.clk(clock_1_out), .Q(counter_1_q));  // open: clr, load, up, count, D, carry
  Decodeur_7_seg decodeur_7_seg_1 (
    .e3(counter_1_q[3]), .e2(counter_1_q[2]), .e1(counter_1_q[1]), .e0(counter_1_q[0]), .a(a_t), .b(b_t),
    .c(c_t), .d(d_t), .e(e_t), .f(f_t), .g(g_t));
  Decodeur_7_seg decodeur_7_seg_2 (
    .e3(counter_1_q[7]), .e2(counter_1_q[6]), .e1(counter_1_q[5]), .e0(counter_1_q[4]), .a(A), .b(B), .c(C),
    .d(D), .e(E), .f(F), .g(G));
  _7_Segment_Display u_7_segment_display_1 (.g(G), .f(F), .a(A), .b(B), .e(E), .d(D), .c(C));  // open: dp
  _7_Segment_Display u_7_segment_display_2 (.g(g_t), .f(f_t), .a(a_t), .b(b_t), .e(e_t), .d(d_t), .c(c_t));  // open: dp

  // Notes on the sheet:
  //   Ceci est un compteur. Activer les ticks dans le menu simulation
  //   placer un splitter
  //   Placer ici le circuit de décodeur 7 segments
  //   Et ici un deuxième décodeur
  //   Placer ici le circuit de décodeur 7 segments
  //   utiliser des tunnels pour connecter 
  //   les sorties du décodeur à l'afficheur
endmodule
