// Logisim project ALU.circ as structural Verilog: 1 circuit, main circuit ALU
module ALU (
  input  [31:0] A,
  input  [31:0] B,
  input  [4:0] Shift,
  input  [3:0] Codop,
  input  CarryIn,
  output [31:0] S,
  output [3:0] Flags
);

  wire f_C_ADC, f_C_ASR, f_C_CMN, f_C_CMP, f_C_LSL, f_C_LSR, f_C_SBC, f_V_ADC, f_V_CMN, f_V_CMP, f_V_SBC,
       not_1_out, subtractor_1_bout, subtractor_2_bout, xnor_1_out, xnor_2_out, xor_2_out, xor_3_out,
       xor_4_out, xor_5_out, xor_6_out, xor_7_out;
  wire [4:0] negator_2_out, subtractor_3_out, subtractor_4_out;
  wire [31:0] CMN_f_entree, CMP_f_entree, i_ADC, i_AND, i_ASR, i_BIC, i_EOR, i_LSL, i_LSR, i_MUL, i_MVN,
       i_ORR, i_ROR, i_RSB, i_SBC, multiplexer_4_out, not_2_out, TST_f_entree;

  assign i_AND = A & B;  // AND_Gate and_1, 32 bits wide
  assign i_EOR = A ^ B;  // XOR_Gate xor_1, 32 bits wide
  Shifter #(.width(32)) shifter_1 (.in(B), .\dist (Shift), .out(i_LSL));
  Shifter #(.shift("lr"), .width(32)) shifter_2 (.in(B), .\dist (Shift), .out(i_LSR));
  Shifter #(.shift("ar"), .width(32)) shifter_3 (.in(B), .\dist (Shift), .out(i_ASR));
  Adder #(.width(32)) adder_1 (.a(A), .b(B), .out(i_ADC), .cin(CarryIn), .cout(f_C_ADC));
  not not_1 (not_1_out, CarryIn);
  Subtractor #(.width(32)) subtractor_1 (.a(B), .b(A), .out(i_SBC), .bin(not_1_out), .bout(subtractor_1_bout));
  Shifter #(.shift("rr"), .width(32)) shifter_4 (.in(B), .\dist (Shift), .out(i_ROR));
  assign TST_f_entree = A & B;  // AND_Gate and_2, 32 bits wide
  Negator #(.width(32)) negator_1 (.in(A), .out(i_RSB));
  Subtractor #(.width(32)) subtractor_2 (.a(B), .b(A), .out(CMP_f_entree), .bout(subtractor_2_bout));  // open: bin
  Adder #(.width(32)) adder_2 (.a(A), .b(B), .out(CMN_f_entree), .cout(f_C_CMN));  // open: cin
  assign i_ORR = A | B;  // OR_Gate or_1, 32 bits wide
  Multiplier #(.width(32)) multiplier_1 (.a(A), .b(B), .out(i_MUL));  // open: cin, cout
  assign not_2_out = ~A;  // NOT_Gate not_2, 32 bits wide
  assign i_BIC = not_2_out & B;  // AND_Gate and_3, 32 bits wide
  assign i_MVN = ~A;  // NOT_Gate not_3, 32 bits wide
  BitSelector #(.width(32)) bitselector_1 (.in(B), .out(f_C_LSL), .sel(negator_2_out));
  Negator #(.width(5)) negator_2 (.in(Shift), .out(negator_2_out));
  BitSelector #(.width(32)) bitselector_2 (.in(B), .out(f_C_LSR), .sel(subtractor_3_out));
  Subtractor #(.width(5)) subtractor_3 (.a(Shift), .b(5'b00001), .out(subtractor_3_out));  // open: bin, bout
  BitSelector #(.width(32)) bitselector_3 (.in(B), .out(f_C_ASR), .sel(subtractor_4_out));
  Subtractor #(.width(5)) subtractor_4 (.a(Shift), .b(5'b00001), .out(subtractor_4_out));  // open: bin, bout
  not not_4 (f_C_SBC, subtractor_1_bout);
  not not_5 (f_C_CMP, subtractor_2_bout);
  Multiplexer #(.enable("false"), .select(4), .width(32)) multiplexer_1 (
    .in0(i_AND), .in1(i_EOR), .in2(i_LSL), .in3(i_LSR), .in4(i_ASR), .in5(i_ADC), .in6(i_SBC), .in7(i_ROR),
    .in8(B), .in9(i_RSB), .in10(B), .in11(B), .in12(i_ORR), .in13(i_MUL), .in14(i_BIC), .in15(i_MVN),
    .out(S), .sel(Codop));
  xor xor_2 (xor_2_out, B[31], S[31]);
  xnor xnor_1 (xnor_1_out, A[31], B[31]);
  xor xor_3 (xor_3_out, B[31], S[31]);
  xor xor_4 (xor_4_out, A[31], B[31]);
  xor xor_5 (xor_5_out, B[31], CMP_f_entree[31]);
  xor xor_6 (xor_6_out, A[31], B[31]);
  xor xor_7 (xor_7_out, B[31], CMN_f_entree[31]);
  xnor xnor_2 (xnor_2_out, A[31], B[31]);
  Multiplexer #(.enable("false"), .select(4)) multiplexer_2 (
    .in0(1'b0), .in1(1'b0), .in2(1'b0), .in3(1'b0), .in4(1'b0), .in5(f_V_ADC), .in6(f_V_SBC), .in7(1'b0),
    .in8(1'b0), .in9(1'b0), .in10(f_V_CMP), .in11(f_V_CMN), .in12(1'b0), .in13(1'b0), .in14(1'b0),
    .in15(1'b0), .out(Flags[0]), .sel(Codop));
  and and_4 (f_V_ADC, xor_2_out, xnor_1_out);
  and and_5 (f_V_SBC, xor_3_out, xor_4_out);
  and and_6 (f_V_CMP, xor_5_out, xor_6_out);
  and and_7 (f_V_CMN, xor_7_out, xnor_2_out);
  Multiplexer #(.enable("false"), .select(4)) multiplexer_3 (
    .in0(1'b0), .in1(1'b0), .in2(f_C_LSL), .in3(f_C_LSR), .in4(f_C_ASR), .in5(f_C_ADC), .in6(f_C_SBC),
    .in7(Flags[3]), .in8(1'b0), .in9(1'b0), .in10(f_C_CMP), .in11(f_C_CMN), .in12(1'b0), .in13(1'b0),
    .in14(1'b0), .in15(1'b0), .out(Flags[1]), .sel(Codop));
  Multiplexer #(.enable("false"), .select(4), .width(32)) multiplexer_4 (
    .in0(S), .in1(S), .in2(S), .in3(S), .in4(S), .in5(S), .in6(S), .in7(S), .in8(TST_f_entree), .in9(S),
    .in10(CMP_f_entree), .in11(CMN_f_entree), .in12(S), .in13(S), .in14(S), .in15(S),
    .out(multiplexer_4_out), .sel(Codop));
  Comparator #(.width(32)) comparator_1 (
    .a(multiplexer_4_out), .b({32{1'b0}}), .eq(Flags[2]), .lt(Flags[3]));  // open: gt

  // Other names for the same wires on the sheet: f_V = Flags[0]; f_C = Flags[1]; f_Z = Flags[2]; f_C_ROR = Flags[3];
  //   f_N = Flags[3]; i_CMN[31:0] = B; i_CMP[31:0] = B; i_TST[31:0] = B

  // Notes on the sheet:
  //   N Z C V
  //   Negative
  //   Zero
  //   Carry
  //   oVerflow
  //   Note: for ROR, C = N
  //   Note 2: assume that shift > 0 for LSL and LSR
endmodule
