// Logisim project BancDeRegistres.circ as structural Verilog: 1 circuit, main circuit BancRegistre
module BancRegistre (
  input  [31:0] DataIn,
  input  [2:0] RegA,
  input  [2:0] RegB,
  input  [2:0] RegDest,
  input  Clk,
  input  Reset,
  output [31:0] AOut,
  output [31:0] BOut,
  output [31:0] R0,
  output [31:0] R1,
  output [31:0] R2,
  output [31:0] R3,
  output [31:0] R4,
  output [31:0] R5,
  output [31:0] R6,
  output [31:0] R7
);
endmodule
