// Logisim project Ctl_Data_Processing.circ as structural Verilog: 2 circuits, main circuit Data_Processing
module Data_Processing (
  input  Enable,
  input  [15:0] Instruction,
  output [2:0] Rd,
  output [2:0] Rn,
  output [2:0] Rm,
  output [3:0] ALU_Opcode,
  output [3:0] Flags_Update_Mask
);

  wire [15:0] bit_extender_1_out;
  wire [15:10] and_1_out;

  assign bit_extender_1_out = {{15{Enable}}, Enable};  // Bit_Extender bit_extender_1
  assign {and_1_out, ALU_Opcode, Rm, Rd} = Instruction & bit_extender_1_out;  // AND_Gate and_1, 16 bits wide
  codop_to_flags_update_mask codop_to_flags_update_mask_1 (.codop(ALU_Opcode), .flags_update_mask(Flags_Update_Mask));

  assign Rn = Rd;

  // Other names for the same wires on the sheet: Rdn[2:0] = Rd; ALU[3:0] = ALU_Opcode

  // Notes on the sheet:
  //   Note 2: RSB instruction has Rn as 1st operand.
  //   MUL instruction has Rn as 1st operand and Rdm as 2nd operand
  //   For simplification purposes, Rm is used for 1st operand both here and in the ALU.
  //   Pull output low on Enable = 0
  //   Note: instructions that does not save the result will still have the second operand as the destination register, the ALU will copy the second register to the destination register
endmodule

module codop_to_flags_update_mask (
  input  [3:0] codop,
  output [3:0] flags_update_mask
);

  wire and_1_out, and_2_out, and_3_out, and_4_out, not_1_out, not_2_out, not_3_out, not_4_out;

  not not_1 (not_1_out, codop[3]);
  not not_2 (not_2_out, codop[2]);
  not not_3 (not_3_out, codop[1]);
  not not_4 (not_4_out, codop[0]);
  or or_1 (flags_update_mask[1], not_1_out, not_2_out, not_4_out, codop[1]);
  and and_1 (and_1_out, not_1_out, codop[2], not_3_out, codop[0]);
  and and_2 (and_2_out, not_1_out, codop[2], codop[1], not_4_out);
  and and_3 (and_3_out, codop[3], not_2_out, codop[0]);
  and and_4 (and_4_out, codop[3], not_2_out, codop[1]);
  or or_2 (flags_update_mask[0], and_1_out, and_2_out, and_3_out, and_4_out);

  assign flags_update_mask[3:2] = 2'b11;
endmodule
