// Logisim project Ctl_Shift_Add_Sub_Mov.circ as structural Verilog: 3 circuits, main circuit Shift_Add_Sub_Mov
module Shift_Add_Sub_Mov (
  input  Enable,
  input  [15:0] Instruction,
  output [3:0] Flags_Update_Mask,
  output Carry,
  output Imm32_Enable,
  output [2:0] Rm,
  output [2:0] Rn,
  output [2:0] Rd,
  output [4:0] Imm5,
  output [31:0] Imm32,
  output [3:0] ALU_Opcode
);

  wire add_i, add_r, and_1_out, and_2_out, and_10_out, and_11_out, i_AD, i_ADD, i_ASR, i_CMP, i_LSL, i_LSR,
       i_MOV, i_SUB, or_1_out, or_2_out, or_3_out, or_4_out, or_5_out, or_9_out, or_10_out, sub_i, sub_r;
  wire [2:0] imm3, Rd1, Rd2, Rd3, Rd4, Rdn5, Rm1, Rm2, Rn1, Rn2;
  wire [3:0] bit_extender_8_out, bit_extender_10_out, flags_to_update_1_flags_update_mask,
       opcode_alu_1_sortie;
  wire [7:0] imm8;
  wire [15:0] and_7_out, and_8_out, bit_extender_1_out, bit_extender_2_out, bit_extender_3_out,
       bit_extender_4_out, bit_extender_5_out, bit_extender_6_out, INST;
  wire [15:9] and_5_out, and_6_out;
  wire [15:11] and_4_out;
  wire [31:0] bit_extender_7_out, bit_extender_9_out, multiplexer_1_out, negator_1_out;

  Decoder #(.select(3)) decoder_1 (
    .out0(i_LSL), .out1(i_LSR), .out2(i_ASR), .out3(i_AD), .out4(i_MOV), .out5(i_CMP), .out6(i_ADD),
    .out7(i_SUB), .sel(INST[13:11]));  // open: en
  Decoder #(.select(2)) decoder_2 (
    .out0(add_r), .out1(sub_r), .out2(add_i), .out3(sub_i), .sel(INST[10:9]));  // open: en
  or or_1 (or_1_out, i_LSL, i_LSR, i_ASR);
  or or_2 (or_2_out, add_r, sub_r);
  or or_3 (or_3_out, add_i, sub_i);
  assign bit_extender_1_out = {{15{Enable}}, Enable};  // Bit_Extender bit_extender_1
  assign bit_extender_2_out = {{15{or_1_out}}, or_1_out};  // Bit_Extender bit_extender_2
  and and_1 (and_1_out, i_AD, or_2_out);
  and and_2 (and_2_out, i_AD, or_3_out);
  or or_4 (or_4_out, i_MOV, i_CMP);
  or or_5 (or_5_out, i_ADD, i_SUB);
  assign INST = Instruction & bit_extender_1_out;  // AND_Gate and_3, 16 bits wide
  assign {and_4_out, Imm5, Rm1, Rd1} = bit_extender_2_out & INST;  // AND_Gate and_4, 16 bits wide
  assign bit_extender_3_out = {{15{and_1_out}}, and_1_out};  // Bit_Extender bit_extender_3
  assign bit_extender_4_out = {{15{and_2_out}}, and_2_out};  // Bit_Extender bit_extender_4
  assign bit_extender_5_out = {{15{or_4_out}}, or_4_out};  // Bit_Extender bit_extender_5
  assign bit_extender_6_out = {{15{or_5_out}}, or_5_out};  // Bit_Extender bit_extender_6
  assign {and_5_out, Rm2, Rn1, Rd2} = bit_extender_3_out & INST;  // AND_Gate and_5, 16 bits wide
  assign {and_6_out, imm3, Rn2, Rd3} = bit_extender_4_out & INST;  // AND_Gate and_6, 16 bits wide
  assign {and_7_out[15:11], Rd4, and_7_out[7:0]} = bit_extender_5_out & INST;  // AND_Gate and_7, 16 bits wide
  assign {and_8_out[15:11], Rdn5, and_8_out[7:0]} = bit_extender_6_out & INST;  // AND_Gate and_8, 16 bits wide
  assign imm8 = and_7_out[7:0] | and_8_out[7:0];  // OR_Gate or_6, 8 bits wide
  assign bit_extender_7_out = {{24{1'b0}}, imm8};  // Bit_Extender bit_extender_7
  Negator #(.width(32)) negator_1 (.in(bit_extender_7_out), .out(negator_1_out));
  assign bit_extender_8_out = {{3{Enable}}, Enable};  // Bit_Extender bit_extender_8
  Flags_To_Update flags_to_update_1 (.codop(INST[13:11]), .flags_update_mask(flags_to_update_1_flags_update_mask));
  assign Rm = Rm1 | Rm2;  // OR_Gate or_7, 3 bits wide
  assign Rn = Rn1 | Rn2 | Rm1 | Rdn5;  // OR_Gate or_8, 3 bits wide
  assign bit_extender_9_out = {{29{1'b0}}, imm3};  // Bit_Extender bit_extender_9
  Multiplexer #(.enable("false"), .width(32)) multiplexer_1 (
    .in0(bit_extender_7_out), .in1(negator_1_out), .out(multiplexer_1_out), .sel(i_MOV));
  or or_9 (or_9_out, sub_i, sub_r);
  or or_10 (or_10_out, add_i, sub_i);
  assign Flags_Update_Mask = bit_extender_8_out & flags_to_update_1_flags_update_mask;  // AND_Gate and_9, 4 bits wide
  assign Rd = Rd1 | Rd2 | Rd3 | Rd4 | Rdn5;  // OR_Gate or_11, 3 bits wide
  assign Imm32 = bit_extender_9_out | multiplexer_1_out;  // OR_Gate or_12, 32 bits wide
  and and_10 (and_10_out, or_9_out, i_AD);
  and and_11 (and_11_out, i_AD, or_10_out);
  opcode_ALU opcode_alu_1 (.Entree(INST[13:9]), .Sortie(opcode_alu_1_sortie));
  assign bit_extender_10_out = {{3{Enable}}, Enable};  // Bit_Extender bit_extender_10
  or or_13 (Carry, and_10_out, i_SUB);
  or or_14 (Imm32_Enable, and_11_out, i_MOV, i_CMP, i_ADD, i_SUB);
  assign ALU_Opcode = opcode_alu_1_sortie & bit_extender_10_out;  // AND_Gate and_12, 4 bits wide

  // Notes on the sheet:
  //   Pull output low on Enable = 0
  //   Enable carry for SUB since it is reversed in ALU
  //   ALU will use Imm32 instead of Rm
  //   only ADD and SUB use Rm
endmodule

module Flags_To_Update (
  input  [2:0] codop,
  output [3:0] flags_update_mask
);

  wire and_1_out, and_2_out, and_3_out, not_1_out;

  not not_1 (not_1_out, codop[2]);
  or or_1 (flags_update_mask[1], not_1_out, codop[0], codop[1]);
  and and_1 (and_1_out, codop[1], codop[0]);
  and and_2 (and_2_out, codop[2], codop[0]);
  and and_3 (and_3_out, codop[2], codop[1]);
  or or_2 (flags_update_mask[0], and_1_out, and_2_out, and_3_out);

  assign flags_update_mask[3:2] = 2'b11;
endmodule

module opcode_ALU (
  input  [4:0] Entree,
  output [3:0] Sortie
);

  wire and_2_out, and_3_out, and_4_out, and_5_out, and_6_out, and_7_out, not_1_out, not_2_out, not_3_out,
       not_4_out;

  not not_1 (not_1_out, Entree[4]);
  not not_2 (not_2_out, Entree[3]);
  not not_3 (not_3_out, Entree[2]);
  not not_4 (not_4_out, Entree[0]);
  and and_1 (Sortie[3], Entree[4], not_2_out);
  and and_2 (and_2_out, not_1_out, not_2_out);
  and and_3 (and_3_out, Entree[2], Entree[0]);
  and and_4 (and_4_out, Entree[4], Entree[2]);
  and and_5 (and_5_out, not_1_out, not_2_out, Entree[2]);
  and and_6 (and_6_out, not_1_out, Entree[2], not_4_out);
  and and_7 (and_7_out, Entree[4], not_3_out);
  or or_1 (Sortie[1], and_2_out, and_3_out, and_4_out);
  or or_2 (Sortie[0], and_5_out, and_6_out, and_7_out);

  assign Sortie[2] = Entree[3];
endmodule
